# Fritzing sketch Pi_motorhader_eg_v_4 (saved by Fritzing 0.9.3b)
circuit board: 6.52541cm x 3.29999cm
breadboards: 1

parts:
  R1 = Resistor [tolerance=±5% resistance=220 package=THT]
  LED1 = LED - 3mm [color="Red (633nm)" package="3 mm [THT]"]
  LED2 = LED - 3mm [color="Red (633nm)" package="3 mm [THT]"]
  LED3 = LED - 3mm [color="Red (633nm)" package="3 mm [THT]"]
  S1 = Pushbutton [package="[THT]"]
  R2 = Resistor [tolerance=±5% resistance=220 package=THT]
  R3 = Resistor [tolerance=±5% resistance=220 package=THT]
  J1 = Raspberry Pi Header 40pin [form="♂ (male)" package=THT]
  SN754410 = H-Bridge [package=THT]
  R4 = Resistor [tolerance=±5% resistance=10k package=THT]
  cool = Pad [width=9 height=4.5 connect=center]
  cool_2 = Pad [width=9 height=4.5 connect=center]
  C1 = Ceramic Capacitor [capacitance=1µF voltage=20V package="100 mil [THT, multilayer]"]
  C2 = Ceramic Capacitor [capacitance=100nF package="100 mil [THT, multilayer]"]
  M1 = Screw terminal - 2 pins [package=THT]
  M2 = Screw terminal - 2 pins [package=THT]
  +_GND = JST-B2P-VH [part_number=JST-B2P-VH package=THT]

nets:
  N1: R1.Pin_0, LED3.anode
  N2: R1.Pin_1, J1.GIPO19
  GND: LED1.cathode, LED2.cathode, LED3.cathode, S1.Pin_1, S1.Pin_2, J1.GND, SN754410.GND1, SN754410.GND2, SN754410.GND3, SN754410.GND4, cool.pad, cool_2.pad, C1.1, C2.1, +_GND.pin2
  N3: LED1.anode, R2.Pin_1
  N4: LED2.anode, R3.Pin_1
  N5: S1.Pin_3, S1.Pin_4, J1.GIPO13
  N6: R2.Pin_0, J1.GIPO4
  N7: R3.Pin_0, J1.GIPO5
  N8: J1.GIPO10, SN754410.4A
  N9: J1.GIPO9, SN754410.3A
  N10: J1.GIPO7, SN754410.1A
  N11: J1.GIPO8, SN754410.2A
  N12: J1.5V, SN754410.VCC1, R4.Pin_0, C2.0
  N13: SN754410.1_2EN, SN754410.3_4EN, R4.Pin_1
  N14: SN754410.1Y, M2.pin2
  N15: SN754410.2Y, M2.pin1
  N16: SN754410.VCC2, +_GND.pin1
  N17: SN754410.3Y, M1.pin2
  N18: SN754410.4Y, M1.pin1

notes:
  erfindergarden
  Pi-Zero Robohead
  V 2.0

custom parts:
  Raspberry Pi Header 40pin: Raspberry Pi 40 pin header - for creating your own shields.
  JST-B2P-VH: JST-B2P-VH Male 2 pin header from JST VH series. The female partner connector (JST-VHR-3N) to this is used on Dagu motors in their robots. This part is not breadboard or stripboard friendly - the pin spacings are not properly compatible. However, you can make the part fit by drilling between the tracks for the outer connectors and soldering a trace across them. This can be represented in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
