# Fritzing sketch Pi_motorhader_simple_v1 (saved by Fritzing 0.9.3b)
circuit board: 6.50001cm x 2.99999cm
breadboards: 1

parts:
  M2 = Screw terminal - 2 pins [package=THT]
  M1 = Screw terminal - 2 pins [package=THT]
  C1 = Ceramic Capacitor [capacitance=1µF voltage=20V package="100 mil [THT, multilayer]"]
  R1 = Resistor [tolerance=±5% resistance=10k package=THT]
  C2 = Ceramic Capacitor [capacitance=100nF package="200 mil [THT, multilayer]"]
  Pad2 = Pad [width=10.371666666666668 height=4.5155555555555553 connect=center]  # not connected
  Pad1 = Pad [width=10.371666666666668 height=4.5155555555555553 connect=center]
  SN754410 = H-Bridge [package=THT]
  Raspberry_Pi_1 = Raspberry Pi 3 [part_number=RPI-3-V1.2]
  J1 = Screw terminal - 2 pins [package=THT]

nets:
  N1: M2.pin1, SN754410.4Y
  N2: M2.pin2, SN754410.3Y
  N3: M1.pin1, SN754410.2Y
  N4: M1.pin2, SN754410.1Y
  N5: C1.0, SN754410.VCC2, J1.pin1
  GND1: C1.1, SN754410.GND1, SN754410.GND2, Raspberry_Pi_1.GND, J1.pin2
  N6: R1.Pin_0, C2.0, Raspberry_Pi_1.5V
  N7: R1.Pin_1, SN754410.1_2EN, SN754410.3_4EN, SN754410.VCC1
  GND3: C2.1, Pad1.pad, SN754410.GND3, SN754410.GND4
  N8: SN754410.1A, Raspberry_Pi_1.GPIO9
  N9: SN754410.2A, Raspberry_Pi_1.GPIO11
  N10: SN754410.3A, Raspberry_Pi_1.GPIO3
  N11: SN754410.4A, Raspberry_Pi_1.GPIO4

notes:
  erfindergarden
  Pi-Zero Robohead
  V 2.0
